// Digital circuit p01 diagrams.dig as structural Verilog
module p01_diagrams (
  input  in_1,
  input  in_3,
  input  in_4,
  input  in_6,
  input  in_7,
  input  in_9,
  input  in_10,
  output out_2,
  output out_5,
  output out_8,
  output out_11
);

  wire nand_2_out, nand_3_out, nand_4_out, nand_5_out, nand_8_out, nand_9_out;

  nand nand_1 (out_2, in_1, in_1);
  nand nand_2 (nand_2_out, in_3, in_4);
  nand nand_3 (nand_3_out, in_6, in_6);
  nand nand_4 (nand_4_out, in_7, in_7);
  nand nand_5 (nand_5_out, in_9, in_10);
  nand nand_6 (out_5, nand_2_out, nand_2_out);
  nand nand_7 (out_8, nand_3_out, nand_4_out);
  nand nand_8 (nand_8_out, in_9, nand_5_out);
  nand nand_9 (nand_9_out, nand_5_out, in_10);
  nand nand_10 (out_11, nand_8_out, nand_9_out);

  // Notes on the sheet:
  //   Not Gate
  //   And Gate
  //   Or Gate
  //   Xor Gate
endmodule
